# Fritzing sketch ESP32-Zero-RFM95W (saved by Fritzing 1.0.1rc)
circuit board: 4.41928cm x 4.35907cm
breadboards: 1

parts:
  A1 = Waveshare esp32-c3-zero smd
  RFM95W1 = RFM95W LoRa Module

nets:
  N1: A1.Pin_2, RFM95W1.1_GND
  N2: A1.Pin_3, RFM95W1.13_3.3V
  N3: A1.Pin_7, RFM95W1.14_DIO0
  N4: A1.Pin_8, RFM95W1.4_SCK
  N5: A1.Pin_9, RFM95W1.2_MISO
  N6: A1.Pin_10, RFM95W1.3_MOSI
  N7: A1.Pin_11, RFM95W1.5_NSS_(CS)
  N8: A1.Pin_12, RFM95W1.6_RESET

custom parts:
  Waveshare esp32-c3-zero smd: ESP32-C3 Mini Development Board, Based on ESP32-C3FN4 Single-core Processor, 160MHz Running Frequency, 2.4GHz Wi-Fi&Bluetooth 5.
  RFM95W LoRa Module: RF Transceiver by Hope RF. Well supported Arduino libraries are available. This Low Power Long Range Transceiver Module for the frequencies 868MHz and 915MHz and it is also available in other versions.
